// Logisim project GuessTheNumber.circ as structural Verilog
module main (
  input  in_1,
  input  in_2,
  input  in_3,
  input  in_4,
  input  in_5,
  input  in_6,
  input  in_7,
  input  in_8
);
endmodule

module game (
  input  Jogar,
  input  A,
  input  B,
  input  Jogador,
  output maior,
  output out_6,
  output igual,
  output menor
);

  mux mux_1 (.A(A), .B(B), .S(Jogador), .C(out_6));
  comparador comparador ();
  // AND_Gate and_1 is placed but not wired
  // AND_Gate and_2 is placed but not wired
  // AND_Gate and_3 is placed but not wired
endmodule

module mux (
  input  A,
  input  B,
  input  S,
  output C
);

  wire and_1_out, and_2_out, not_1_out;

  not not_1 (not_1_out, S);
  and and_1 (and_1_out, not_1_out, A);
  and and_2 (and_2_out, S, B);
  or or_1 (C, and_1_out, and_2_out);
endmodule
